# Fritzing sketch motor-driver (saved by Fritzing 0.9.4)
breadboards: 1

parts:
  S1 = H-Bridge with L298N
  Part1 = Arduino Uno (Rev3) - ICSP
  M1 = DC Motor
  M2 = DC Motor
  R1 = Resistor [tolerance=±5% resistance=10k package=THT]
  R2 = Resistor [tolerance=±5% resistance=10k package=THT]
  S2 = Pushbutton [package="[THT]"]
  S3 = Pushbutton [package="[THT]"]

nets:
  GND: S1.GND, Part1.GND, R1.Pin_1, R2.Pin_1
  N1: S1.ENA, S1.ENA-5V
  N2: S1.IN1, Part1.D12/MISO
  N3: S1.IN2, Part1.D11_PWM/MOSI
  N4: S1.IN3, Part1.D10_PWM/SS
  N5: S1.IN4, Part1.D9_PWM
  N6: S1.ENB, S1.ENB-5V
  N7: S1.M1-01, M1.pin_2
  N8: S1.M1-02, M1.pin_1
  N9: S1.M2-01, M2.pin_2
  N10: S1.M2-02, M2.pin_1
  N11: Part1.D3_PWM, R1.Pin_0, S2.Pin_1, S2.Pin_2
  N12: Part1.D4, R2.Pin_0, S3.Pin_1, S3.Pin_2
  N13: Part1.5V, S2.Pin_3, S2.Pin_4, S3.Pin_3, S3.Pin_4

notes:
  From 5v output of the powerbank
  From 12v output of the powerbank

custom parts:
  H-Bridge with L298N: h-bridge
